# Fritzing sketch exec-02 (saved by Fritzing 1.0.2b)
breadboards: 1

parts:
  A2 = Raspberry Pi Pico W
  LED1 = smd LED [color="Red (633nm)" package="1206 [SMD]"]
  R1 = Resistor [tolerance=±5% power=0.25W resistance=220 package=THT]
  LED2 = smd LED [color="Red (633nm)" package="1206 [SMD]"]
  R2 = Resistor [tolerance=±5% power=0.25W resistance=220 package=THT]
  LED3 = smd LED [color="Red (633nm)" package="1206 [SMD]"]
  R3 = Resistor [tolerance=±5% power=0.25W resistance=220 package=THT]
  LED4 = smd LED [color="Red (633nm)" package="1206 [SMD]"]
  R4 = Resistor [tolerance=±5% power=0.25W resistance=220 package=THT]

nets:
  N1: A2.pin_3, A2.pin_8, A2.pin_13, A2.pin_18, A2.pin_23, A2.pin_28, A2.pin_33, A2.pin_38, A2.pin_42, R1.Pin_0, R2.Pin_0, R3.Pin_0, R4.Pin_0
  N2: A2.pin_16, LED4.anode
  N3: A2.pin_17, LED3.anode
  N4: A2.pin_19, LED2.anode
  N5: A2.pin_20, LED1.anode
  N6: LED1.cathode, R1.Pin_1
  N7: LED2.cathode, R2.Pin_1
  N8: LED3.cathode, R3.Pin_1
  N9: LED4.cathode, R4.Pin_1

custom parts:
  Raspberry Pi Pico W: Raspberry Pi Pico W. Based around the RP2040 microcontroller the Pico W is a low cost microcontroller device bringing Raspberry Pi quality, cost, and easy of use to the microcontroller space. The areas marked KEEPOUT in pcb silkscreen should not have traces running through them to avoid shorts on a soldered in module!
